# Fritzing sketch ntut_counterculture_04 (saved by Fritzing 0.9.3b)
breadboards: 2

parts:
  S2 = Round Pushbutton
  LED1 = smd LED [color="Green (555nm)" package="0603 [SMD]"]
  C1 = Tantalum Capacitor [capacitance=1μF package="100 mil [THT, tantalum]"]
  C2 = Electrolytic Capacitor [capacitance=1µF package="100 mil [THT, electrolytic]"]
  C3 = Ceramic Capacitor [capacitance=100nF package="100 mil [THT, multilayer]"]
  Q2 = NPN-Transistor [package="TO92 [THT]"]
  SPKR1 = Loudspeaker
  S4 = Toggle Switch [package=THT]
  U2 = LM386 [package=dip08]
  R2 = Rotary Potentiometer (Large) [maximum_resistance=10kΩ package=THT]
  C4 = Ceramic Capacitor [capacitance=100nF package="100 mil [THT, multilayer]"]
  R3 = Resistor [tolerance=±5% resistance=10 package="0402 [SMD]"]
  Q3 = NPN-Transistor [package="TO92 [THT]"]
  Q4 = NPN-Transistor [package="TO92 [THT]"]
  Q5 = NPN-Transistor [package="TO92 [THT]"]
  Q6 = NPN-Transistor [package="TO92 [THT]"]
  Q7 = NPN-Transistor [package="TO92 [THT]"]
  R11 = Resistor [tolerance=±5% resistance=1k package="0402 [SMD]"]
  R14 = Resistor [tolerance=±5% resistance=680 package="0402 [SMD]"]
  R15 = Resistor [tolerance=±5% resistance=1k package="0402 [SMD]"]
  R16 = Resistor [tolerance=±5% resistance=1k package="0402 [SMD]"]
  R17 = Resistor [tolerance=±5% resistance=1k package="0402 [SMD]"]
  R18 = Resistor [tolerance=±5% resistance=1k package="0402 [SMD]"]
  R19 = Resistor [tolerance=±5% resistance=1k package="0402 [SMD]"]
  R20 = Resistor [tolerance=±5% resistance=680 package="0402 [SMD]"]
  R21 = Resistor [tolerance=±5% resistance=680 package="0402 [SMD]"]
  R22 = Resistor [tolerance=±5% resistance=680 package="0402 [SMD]"]
  R23 = Resistor [tolerance=±5% resistance=680 package="0402 [SMD]"]
  R24 = Resistor [tolerance=±5% resistance=680 package="0402 [SMD]"]
  7_Segment1 = 7 Segment Display
  TRRS1 = Audio Jack (TRRS) 3.5mm [part_number="LUMBERG JEITA RC-5325A" package="RC-5325A [SMD]"]
  R25 = Resistor [tolerance=±5% resistance=4.7k package="0402 [SMD]"]  # not connected
  Part1 = Arduino Mega 2560 (Rev3)
  VCC1 = Battery block 9V
  R26 = Rotary Potentiometer (Large) [maximum_resistance=100kΩ package=THT]  # not connected
  VCC2 = Battery block 9V
  S5 = SWITCH-DPDT [package=ms]
  S7 = Pushbutton [package="[SMD]"]
  S9 = Toggle Switch [package=THT]
  R27 = Resistor [tolerance=±5% resistance=1k package="0402 [SMD]"]
  R28 = Resistor [tolerance=±5% resistance=1k package="0402 [SMD]"]  # not connected
  R29 = Resistor [tolerance=±5% resistance=1k package="0402 [SMD]"]  # not connected
  R30 = Resistor [tolerance=±5% resistance=1k package="0402 [SMD]"]  # not connected
  R31 = Resistor [tolerance=±5% resistance=1k package="0402 [SMD]"]
  R32 = Resistor [tolerance=±5% resistance=1k package="0402 [SMD]"]
  R33 = Resistor [tolerance=±5% resistance=680 package="0402 [SMD]"]
  Q8 = NPN-Transistor [package="TO92 [THT]"]
  Part2 = MicroSD Card Module

nets:
  N1: S2.leg0, Part1.D2_PWM, S7.Pin_1, S7.Pin_2
  N2: S2.leg1, LED1.cathode, Q2.C, Q3.C, Q4.C, Q5.C, Q6.C, Q7.C, VCC2.+, S5.5, S7.Pin_3, S7.Pin_4, Q8.C
  N3: C1.-, C3.0, U2.OUT
  N4: C1.+, S4.L2, TRRS1.TIP
  N5: C2.-, C2.+, U2.GAIN
  N6: C3.1, R3.Pin_0
  N7: Q2.E, R19.Pin_0
  N8: Q2.B, R20.Pin_0
  GND: SPKR1.pin1, U2.-IN, U2.V-, R2.wiper, R2.leg2, R3.Pin_1, TRRS1.SLEEVE, Part1.GND, S9.COM, R31.Pin_1, Part2.GND
  N9: SPKR1.pin2, S4.COM
  5V: U2.V+, Part1.5V, R27.Pin_0, Part2.VCC
  N10: R2.leg1, C4.0
  N11: C4.1, Part1.D11_PWM
  N12: Q3.E, R18.Pin_0
  N13: Q3.B, R21.Pin_0
  N14: Q4.E, R17.Pin_0
  N15: Q4.B, R22.Pin_0
  N16: Q5.E, R16.Pin_0
  N17: Q5.B, R23.Pin_0
  N18: Q6.E, R11.Pin_0
  N19: Q6.B, R14.Pin_0
  N20: Q7.E, R15.Pin_0
  N21: Q7.B, R24.Pin_0
  N22: R11.Pin_1, 7_Segment1.Segment_F
  N23: R14.Pin_1, Part1.D26
  N24: R15.Pin_1, 7_Segment1.Segment_A
  N25: R16.Pin_1, 7_Segment1.Segment_B
  N26: R17.Pin_1, 7_Segment1.Segment_E
  N27: R18.Pin_1, 7_Segment1.Segment_D
  N28: R19.Pin_1, 7_Segment1.Segment_C
  N29: R20.Pin_1, Part1.D36
  N30: R21.Pin_1, Part1.D30
  N31: R22.Pin_1, Part1.D34
  N32: R23.Pin_1, Part1.D32
  N33: R24.Pin_1, Part1.D28
  N34: 7_Segment1.Segment_G, R32.Pin_1
  N35: Part1.D7_PWM, S9.L1
  N36: Part1.D24, R33.Pin_1
  N37: Part1.D50, Part2.MISO
  N38: Part1.D51, Part2.MOSI
  N39: Part1.D52, Part2.SCK
  N40: Part1.D53, Part2.CS
  N41: VCC1.+, S5.1
  N42: R32.Pin_0, Q8.E
  N43: R33.Pin_0, Q8.B

notes:
  6 position rotary switch (SRRN162)
  and resistor ladder
  → language selector
  250 µF
  10 µF
  0.05 µF
  AMPLIFIER
  3.5mm audio jack
  switch
  → speaker on
  → speaker off
  switch
  → random
  → consecutive
  Giant DPDT rocker switch
  LED
  inside arcade pushbutton
  10 | 09 | 08 | 07 | 06 | 05 | 04
  8Ω | 3W
  Micro SD card adapter with 16kHz unsigned 8 bit pcm .wav tracks on SD card.
  10kΩ
  #1
  #10
